// Logisim project P0.Q1.circ as structural Verilog: 6 circuits, main circuit CRC
module CRC (
  input  [7:0] in_1,
  input  [3:0] in_2,
  output [10:0] out_3
);

  divide divide_1 (.in_1({in_1, 3'b000}), .in_2(in_2), .out_3(out_3[2:0]));

  assign out_3[10:3] = in_1;
endmodule

module divide (
  input  [10:0] in_1,
  input  [3:0] in_2,
  output [2:0] out_3
);

  wire [3:0] function_process_1_out_4, function_process_2_out_4, function_process_3_out_4,
       function_process_4_out_4, function_process_5_out_4, function_process_6_out_4, function_process_7_out_4;

  function_process function_process_1 (
    .in_1(in_1[10:7]), .in_2(in_2), .in_3(in_1[6]), .out_4(function_process_1_out_4));
  function_process function_process_2 (
    .in_1(function_process_1_out_4), .in_2(in_2), .in_3(in_1[5]), .out_4(function_process_2_out_4));
  function_process function_process_3 (
    .in_1(function_process_2_out_4), .in_2(in_2), .in_3(in_1[4]), .out_4(function_process_3_out_4));
  function_process function_process_4 (
    .in_1(function_process_3_out_4), .in_2(in_2), .in_3(in_1[3]), .out_4(function_process_4_out_4));
  function_process function_process_5 (
    .in_1(function_process_4_out_4), .in_2(in_2), .in_3(in_1[2]), .out_4(function_process_5_out_4));
  function_process function_process_6 (
    .in_1(function_process_5_out_4), .in_2(in_2), .in_3(in_1[1]), .out_4(function_process_6_out_4));
  function_process function_process_7 (
    .in_1(function_process_6_out_4), .in_2(in_2), .in_3(in_1[0]), .out_4(function_process_7_out_4));
  function_end function_end_1 (.in_1(function_process_7_out_4), .in_2(in_2), .out_3(out_3));

  // Other names for the same wires on the sheet: step8 = in_1[0]; step7 = in_1[1]; step6 = in_1[2]; step5 = in_1[3];
  //   step4 = in_1[4]; step3 = in_1[5]; step2 = in_1[6]; step1[3:0] = in_1[10:7]
endmodule

module XOR (
  input  [3:0] in_1,
  input  [3:0] in_2,
  output [2:0] out_3
);

  xor xor_1 (out_3[0], in_1[0], in_2[0]);
  xor xor_2 (out_3[1], in_1[1], in_2[1]);
  xor xor_3 (out_3[2], in_1[2], in_2[2]);
endmodule

module check (
  input  [3:0] in_1,
  input  [3:0] in_2,
  output [3:0] out_3
);

  wire comparator_1_eq;

  Comparator #(.width(1)) comparator_1 (.a(in_1[3]), .b(1'b1), .eq(comparator_1_eq));  // open: gt, lt
  Multiplexer #(.width(4)) multiplexer_1 (.in0(4'b0000), .in1(in_2), .out(out_3), .sel(comparator_1_eq));  // open: en
endmodule

module function_process (
  input  [3:0] in_1,
  input  [3:0] in_2,
  input  in_3,
  output [3:0] out_4
);

  wire [3:0] check_1_out_3;

  check check_1 (.in_1(in_1), .in_2(in_2), .out_3(check_1_out_3));
  XOR xor_1 (.in_1(in_1), .in_2(check_1_out_3), .out_3(out_4[3:1]));

  assign out_4[0] = in_3;
endmodule

module function_end (
  input  [3:0] in_1,
  input  [3:0] in_2,
  output [2:0] out_3
);

  wire [3:0] check_1_out_3;

  check check_1 (.in_1(in_1), .in_2(in_2), .out_3(check_1_out_3));
  XOR xor_1 (.in_1(in_1), .in_2(check_1_out_3), .out_3(out_3));
endmodule
