// Logisim project P0.Q2.circ as structural Verilog: 1 circuit, main circuit grf
module grf (
  input  in_1,
  input  in_2,
  input  in_3,
  input  [4:0] A1,
  input  [4:0] A2,
  input  [4:0] A3,
  input  [31:0] WD,
  output [31:0] RD1,
  output [31:0] RD2
);

  wire [31:0] in1, in2, in3, in4, in5, in6, in7, in8, in9, in10, in11, in12, in13, in14, in15, in16, in17,
       in18, in19, in20, in21, in22, in23, in24, in25, in26, in27, in28, in29, in30, in31, in32, out1, out2,
       out3, out4, out5, out6, out7, out8, out9, out10, out11, out12, out13, out14, out15, out16, out17,
       out18, out19, out20, out21, out22, out23, out24, out25, out26, out27, out28, out29, out30, out31,
       out32;

  Demultiplexer #(.select(5), .width(32), .tristate("true")) demultiplexer_1 (
    .out0(in1), .out1(in2), .out2(in3), .out3(in4), .out4(in5), .out5(in6), .out6(in7), .out7(in8),
    .out8(in9), .out9(in10), .out10(in11), .out11(in12), .out12(in13), .out13(in14), .out14(in15),
    .out15(in16), .out16(in17), .out17(in18), .out18(in19), .out19(in20), .out20(in21), .out21(in22),
    .out22(in23), .out23(in24), .out24(in25), .out25(in26), .out26(in27), .out27(in28), .out28(in29),
    .out29(in30), .out30(in31), .out31(in32), .in(WD), .sel(A3), .en(in_3));
  Multiplexer #(.select(5), .width(32)) multiplexer_1 (
    .in0(out1), .in1(out2), .in2(out3), .in3(out4), .in4(out5), .in5(out6), .in6(out7), .in7(out8),
    .in8(out9), .in9(out10), .in10(out11), .in11(out12), .in12(out13), .in13(out14), .in14(out15),
    .in15(out16), .in16(out17), .in17(out18), .in18(out19), .in19(out20), .in20(out21), .in21(out22),
    .in22(out23), .in23(out24), .in24(out25), .in25(out26), .in26(out27), .in27(out28), .in28(out29),
    .in29(out30), .in30(out31), .in31(out32), .out(RD1), .sel(A1));  // open: en
  Multiplexer #(.select(5), .width(32)) multiplexer_2 (
    .in0(out1), .in1(out2), .in2(out3), .in3(out4), .in4(out5), .in5(out6), .in6(out7), .in7(out8),
    .in8(out9), .in9(out10), .in10(out11), .in11(out12), .in12(out13), .in13(out14), .in14(out15),
    .in15(out16), .in16(out17), .in17(out18), .in18(out19), .in19(out20), .in20(out21), .in21(out22),
    .in22(out23), .in23(out24), .in24(out25), .in25(out26), .in26(out27), .in27(out28), .in28(out29),
    .in29(out30), .in30(out31), .in31(out32), .out(RD2), .sel(A2));  // open: en
  Register #(.width(32)) r1 (.D(in1), .en(1'b0), .Q(out1), .clk(in_1), .clr(in_2));
  Register #(.width(32)) r2 (.D(in2), .Q(out2), .clk(in_1), .clr(in_2));  // open: en
  Register #(.width(32)) r3 (.D(in3), .Q(out3), .clk(in_1), .clr(in_2));  // open: en
  Register #(.width(32)) r4 (.D(in4), .Q(out4), .clk(in_1), .clr(in_2));  // open: en
  Register #(.width(32)) r5 (.D(in5), .Q(out5), .clk(in_1), .clr(in_2));  // open: en
  Register #(.width(32)) r6 (.D(in6), .Q(out6), .clk(in_1), .clr(in_2));  // open: en
  Register #(.width(32)) r7 (.D(in7), .Q(out7), .clk(in_1), .clr(in_2));  // open: en
  Register #(.width(32)) r8 (.D(in8), .Q(out8), .clk(in_1), .clr(in_2));  // open: en
  Multiplexer #(.width(32)) multiplexer_3 ();  // open: in0, in1, out, sel, en
  Register #(.width(32)) r9 (.D(in9), .Q(out9), .clk(in_1), .clr(in_2));  // open: en
  Register #(.width(32)) r10 (.D(in10), .Q(out10), .clk(in_1), .clr(in_2));  // open: en
  Register #(.width(32)) r11 (.D(in11), .Q(out11), .clk(in_1), .clr(in_2));  // open: en
  Register #(.width(32)) r12 (.D(in12), .Q(out12), .clk(in_1), .clr(in_2));  // open: en
  Register #(.width(32)) r13 (.D(in13), .Q(out13), .clk(in_1), .clr(in_2));  // open: en
  Register #(.width(32)) r14 (.D(in14), .Q(out14), .clk(in_1), .clr(in_2));  // open: en
  Register #(.width(32)) r15 (.D(in15), .Q(out15), .clk(in_1), .clr(in_2));  // open: en
  Register #(.width(32)) r16 (.D(in16), .Q(out16), .clk(in_1), .clr(in_2));  // open: en
  Register #(.width(32)) r17 (.D(in17), .Q(out17), .clk(in_1), .clr(in_2));  // open: en
  Register #(.width(32)) r18 (.D(in18), .Q(out18), .clk(in_1), .clr(in_2));  // open: en
  Register #(.width(32)) r19 (.D(in19), .Q(out19), .clk(in_1), .clr(in_2));  // open: en
  Register #(.width(32)) r20 (.D(in20), .Q(out20), .clk(in_1), .clr(in_2));  // open: en
  Register #(.width(32)) r21 (.D(in21), .Q(out21), .clk(in_1), .clr(in_2));  // open: en
  Register #(.width(32)) r22 (.D(in22), .Q(out22), .clk(in_1), .clr(in_2));  // open: en
  Register #(.width(32)) r23 (.D(in23), .Q(out23), .clk(in_1), .clr(in_2));  // open: en
  Register #(.width(32)) r24 (.D(in24), .Q(out24), .clk(in_1), .clr(in_2));  // open: en
  Register #(.width(32)) r25 (.D(in25), .Q(out25), .clk(in_1), .clr(in_2));  // open: en
  Register #(.width(32)) r26 (.D(in26), .Q(out26), .clk(in_1), .clr(in_2));  // open: en
  Register #(.width(32)) r27 (.D(in27), .Q(out27), .clk(in_1), .clr(in_2));  // open: en
  Register #(.width(32)) r28 (.D(in28), .Q(out28), .clk(in_1), .clr(in_2));  // open: en
  Register #(.width(32)) r29 (.D(in29), .Q(out29), .clk(in_1), .clr(in_2));  // open: en
  Register #(.width(32)) r30 (.D(in30), .Q(out30), .clk(in_1), .clr(in_2));  // open: en
  Register #(.width(32)) r31 (.D(in31), .Q(out31), .clk(in_1), .clr(in_2));  // open: en
  Register #(.width(32)) r32 (.D(in32), .Q(out32), .clk(in_1), .clr(in_2));  // open: en

  // Other names for the same wires on the sheet: clk = in_1; reset = in_2; WE = in_3
endmodule
