// Logisim project P0.Q2.new.circ as structural Verilog
module grf (
  input  clk,
  input  resrt,
  input  WE,
  input  [4:0] A1,
  input  [4:0] A2,
  input  [4:0] A3,
  input  [31:0] WD,
  output [31:0] out_8,
  output [31:0] out_9
);

  wire W0, W1, W2, W3, W4, W5, W6, W7, W8, W9, W10, W11, W12, W13, W14, W15, W16, W17, W18, W19, W20, W21,
       W22, W23, W24, W25, W26, W27, W28, W29, W30, W31;
  wire [31:0] out0, out1, out2, out3, out4, out5, out6, out7, out8, out9, out10, out11, out12, out13, out14,
       out15, out16, out17, out18, out19, out20, out21, out22, out23, out24, out25, out26, out27, out28,
       out29, out30, out31;

  Demultiplexer #(.select(5)) demultiplexer_1 (
    .out0(W0), .out1(W1), .out2(W2), .out3(W3), .out4(W4), .out5(W5), .out6(W6), .out7(W7), .out8(W8),
    .out9(W9), .out10(W10), .out11(W11), .out12(W12), .out13(W13), .out14(W14), .out15(W15), .out16(W16),
    .out17(W17), .out18(W18), .out19(W19), .out20(W20), .out21(W21), .out22(W22), .out23(W23), .out24(W24),
    .out25(W25), .out26(W26), .out27(W27), .out28(W28), .out29(W29), .out30(W30), .out31(W31), .in(WE),
    .sel(A3));  // open: en
  Register #(.width(32)) register_1 (.D({32{1'b0}}), .en(W0), .Q(out0), .clk(clk), .clr(resrt));
  Register #(.width(32)) register_2 (.D(WD), .en(W1), .Q(out1), .clk(clk), .clr(resrt));
  Register #(.width(32)) register_3 (.D(WD), .en(W2), .Q(out2), .clk(clk), .clr(resrt));
  Register #(.width(32)) register_4 (.D(WD), .en(W3), .Q(out3), .clk(clk), .clr(resrt));
  Register #(.width(32)) register_5 (.D(WD), .en(W4), .Q(out4), .clk(clk), .clr(resrt));
  Register #(.width(32)) register_6 (.D(WD), .en(W5), .Q(out5), .clk(clk), .clr(resrt));
  Register #(.width(32)) register_7 (.D(WD), .en(W6), .Q(out6), .clk(clk), .clr(resrt));
  Register #(.width(32)) register_8 (.D(WD), .en(W7), .Q(out7), .clk(clk), .clr(resrt));
  Register #(.width(32)) register_9 (.D(WD), .en(W8), .Q(out8), .clk(clk), .clr(resrt));
  Register #(.width(32)) register_10 (.D(WD), .en(W9), .Q(out9), .clk(clk), .clr(resrt));
  Register #(.width(32)) register_11 (.D(WD), .en(W10), .Q(out10), .clk(clk), .clr(resrt));
  Register #(.width(32)) register_12 (.D(WD), .en(W11), .Q(out11), .clk(clk), .clr(resrt));
  Register #(.width(32)) register_13 (.D(WD), .en(W12), .Q(out12), .clk(clk), .clr(resrt));
  Register #(.width(32)) register_14 (.D(WD), .en(W13), .Q(out13), .clk(clk), .clr(resrt));
  Register #(.width(32)) register_15 (.D(WD), .en(W14), .Q(out14), .clk(clk), .clr(resrt));
  Register #(.width(32)) register_16 (.D(WD), .en(W15), .Q(out15), .clk(clk), .clr(resrt));
  Register #(.width(32)) register_17 (.D(WD), .en(W16), .Q(out16), .clk(clk), .clr(resrt));
  Register #(.width(32)) register_18 (.D(WD), .en(W17), .Q(out17), .clk(clk), .clr(resrt));
  Register #(.width(32)) register_19 (.D(WD), .en(W18), .Q(out18), .clk(clk), .clr(resrt));
  Register #(.width(32)) register_20 (.D(WD), .en(W19), .Q(out19), .clk(clk), .clr(resrt));
  Register #(.width(32)) register_21 (.D(WD), .en(W20), .Q(out20), .clk(clk), .clr(resrt));
  Register #(.width(32)) register_22 (.D(WD), .en(W21), .Q(out21), .clk(clk), .clr(resrt));
  Register #(.width(32)) register_23 (.D(WD), .en(W22), .Q(out22), .clk(clk), .clr(resrt));
  Register #(.width(32)) register_24 (.D(WD), .en(W23), .Q(out23), .clk(clk), .clr(resrt));
  Register #(.width(32)) register_25 (.D(WD), .en(W24), .Q(out24), .clk(clk), .clr(resrt));
  Register #(.width(32)) register_26 (.D(WD), .en(W25), .Q(out25), .clk(clk), .clr(resrt));
  Register #(.width(32)) register_27 (.D(WD), .en(W26), .Q(out26), .clk(clk), .clr(resrt));
  Register #(.width(32)) register_28 (.D(WD), .en(W27), .Q(out27), .clk(clk), .clr(resrt));
  Register #(.width(32)) register_29 (.D(WD), .en(W28), .Q(out28), .clk(clk), .clr(resrt));
  Register #(.width(32)) register_30 (.D(WD), .en(W29), .Q(out29), .clk(clk), .clr(resrt));
  Register #(.width(32)) register_31 (.D(WD), .en(W30), .Q(out30), .clk(clk), .clr(resrt));
  Register #(.width(32)) register_32 (.D(WD), .en(W31), .Q(out31), .clk(clk), .clr(resrt));
  Multiplexer #(.select(5), .width(32)) multiplexer_1 (
    .in0(out0), .in1(out1), .in2(out2), .in3(out3), .in4(out4), .in5(out5), .in6(out6), .in7(out7),
    .in8(out8), .in9(out9), .in10(out10), .in11(out11), .in12(out12), .in13(out13), .in14(out14),
    .in15(out15), .in16(out16), .in17(out17), .in18(out18), .in19(out19), .in20(out20), .in21(out21),
    .in22(out22), .in23(out23), .in24(out24), .in25(out25), .in26(out26), .in27(out27), .in28(out28),
    .in29(out29), .in30(out30), .in31(out31), .out(out_8), .sel(A1));  // open: en
  Multiplexer #(.select(5), .width(32)) multiplexer_2 (
    .in0(out0), .in1(out1), .in2(out2), .in3(out3), .in4(out4), .in5(out5), .in6(out6), .in7(out7),
    .in8(out8), .in9(out9), .in10(out10), .in11(out11), .in12(out12), .in13(out13), .in14(out14),
    .in15(out15), .in16(out16), .in17(out17), .in18(out18), .in19(out19), .in20(out20), .in21(out21),
    .in22(out22), .in23(out23), .in24(out24), .in25(out25), .in26(out26), .in27(out27), .in28(out28),
    .in29(out29), .in30(out30), .in31(out31), .out(out_9), .sel(A2));  // open: en

  // Other names for the same wires on the sheet: RD1[31:0] = out_8; RD2[31:0] = out_9; reset = resrt
endmodule
