// Logisim project P0.Q3.circ as structural Verilog: 4 circuits, main circuit navigation
module navigation (
  input  [1:0] dir,
  input  clk,
  input  reset,
  output arrive,
  output hit
);

  wire save_1_out_7, save_1_out_8, save_1_out_9, transfer_1_a0, transfer_1_a1, transfer_1_a2, transfer_1_hit;

  transfer transfer_1 (
    .s2(save_1_out_7), .s1(save_1_out_8), .s0(save_1_out_9), .d1(dir[1]), .d0(dir[0]), .a2(transfer_1_a2),
    .a1(transfer_1_a1), .a0(transfer_1_a0), .hit(transfer_1_hit));
  save save_1 (
    .s2(transfer_1_a2), .s1(transfer_1_a1), .s0(transfer_1_a0), .out_7(save_1_out_7), .out_8(save_1_out_8),
    .out_9(save_1_out_9), .in_5(clk), .in_6(reset), .hit(transfer_1_hit), .out_10(hit));
  \output  output_1 (.s2(save_1_out_7), .s1(save_1_out_8), .s0(save_1_out_9), .arrive(arrive));
endmodule

module transfer (
  input  s2,
  input  s1,
  input  s0,
  input  d1,
  input  d0,
  output a2,
  output a1,
  output a0,
  output hit
);

  wire and_1_out, and_2_out, and_3_out, and_4_out, and_5_out, and_6_out, and_7_out, and_8_out, and_9_out,
       and_10_out, and_11_out, and_12_out, and_13_out, and_14_out, and_15_out, and_16_out, not_1_out,
       not_2_out, not_3_out, not_4_out, not_5_out, not_6_out, not_7_out, not_8_out, not_9_out, not_10_out,
       not_11_out, not_12_out, not_13_out, not_14_out, not_15_out, not_16_out, not_17_out, not_18_out,
       not_19_out, not_20_out, not_21_out, not_22_out, not_23_out, not_24_out, not_25_out, not_26_out,
       not_27_out, not_28_out;

  not not_1 (not_1_out, s0);
  not not_2 (not_2_out, d1);
  not not_3 (not_3_out, d0);
  not not_4 (not_4_out, d1);
  not not_5 (not_5_out, s1);
  not not_6 (not_6_out, d1);
  not not_7 (not_7_out, d1);
  not not_8 (not_8_out, d0);
  not not_9 (not_9_out, s0);
  not not_10 (not_10_out, d1);
  not not_11 (not_11_out, s0);
  not not_12 (not_12_out, d0);
  not not_13 (not_13_out, s2);
  not not_14 (not_14_out, s1);
  not not_15 (not_15_out, d1);
  not not_16 (not_16_out, d0);
  not not_17 (not_17_out, d0);
  not not_18 (not_18_out, s2);
  not not_19 (not_19_out, s0);
  not not_20 (not_20_out, d1);
  not not_21 (not_21_out, s2);
  not not_22 (not_22_out, s1);
  not not_23 (not_23_out, s0);
  not not_24 (not_24_out, s2);
  not not_25 (not_25_out, s0);
  not not_26 (not_26_out, d0);
  not not_27 (not_27_out, d1);
  not not_28 (not_28_out, d0);
  and and_1 (and_1_out, s1, not_1_out, not_2_out, not_3_out);
  and and_2 (and_2_out, s1, s0, not_4_out, d0);
  and and_3 (and_3_out, not_5_out, s0, not_6_out);
  and and_4 (and_4_out, s0, not_7_out, not_8_out);
  and and_5 (and_5_out, s1, not_9_out, not_10_out, d0);
  and and_6 (and_6_out, s1, not_11_out, d1, not_12_out);
  and and_7 (and_7_out, s1, s0, d1, d0);
  and and_8 (and_8_out, not_13_out, not_14_out, not_15_out, not_16_out);
  and and_9 (and_9_out, s0, d1, d0);
  and and_10 (and_10_out, s1, d1, d0);
  and and_11 (and_11_out, s1, s0, not_17_out);
  and and_12 (and_12_out, not_18_out, not_19_out, not_20_out, d0);
  and and_13 (and_13_out, not_21_out, not_22_out, not_23_out, d1);
  and and_14 (and_14_out, not_24_out, not_25_out, d1, not_26_out);
  and and_15 (and_15_out, s0, d1, d0);
  and and_16 (and_16_out, s1, s0, not_27_out, not_28_out);
  or or_1 (a2, and_1_out, and_2_out);
  or or_2 (a1, and_3_out, and_4_out, and_5_out, and_6_out, and_7_out);
  or or_3 (a0, and_8_out, and_9_out, and_10_out, and_11_out);
  or or_4 (hit, and_12_out, and_13_out, and_14_out, and_15_out, and_16_out);
endmodule

module save (
  input  s2,
  input  s1,
  input  s0,
  input  hit,
  input  in_5,
  input  in_6,
  output out_7,
  output out_8,
  output out_9,
  output out_10
);

  Register #(.width(1)) register_1 (.D(s2), .Q(out_7), .clk(in_5), .clr(in_6));  // open: en
  Register #(.width(1)) register_2 (.D(s1), .Q(out_8), .clk(in_5), .clr(in_6));  // open: en
  Register #(.width(1)) register_3 (.D(s0), .Q(out_9), .clk(in_5), .clr(in_6));  // open: en
  Register #(.width(1)) register_4 (.D(hit), .Q(out_10), .clk(in_5), .clr(in_6));  // open: en
endmodule

module \output  (
  input  s2,
  input  s1,
  input  s0,
  output arrive
);

  wire not_1_out, not_2_out;

  not not_1 (not_1_out, s1);
  not not_2 (not_2_out, s0);
  and and_1 (arrive, s2, not_1_out, not_2_out);
endmodule
