// Logisim project P0.Q4.circ as structural Verilog: 4 circuits, main circuit fsm
module fsm (
  input  CLR,
  input  [1:0] In,
  output z
);

  wire clock_1_out, save_1_out_5, save_1_out_6, transfer_1_a0, transfer_1_a1;

  transfer transfer_1 (
    .s1(save_1_out_5), .s0(save_1_out_6), .i1(In[1]), .i0(In[0]), .a1(transfer_1_a1), .a0(transfer_1_a0));
  save save_1 (
    .in_1(transfer_1_a1), .in_2(transfer_1_a0), .in_3(CLR), .in_4(clock_1_out), .out_5(save_1_out_5),
    .out_6(save_1_out_6));
  Clock clock_1 (.out(clock_1_out));
  \output  output_1 (.s1(save_1_out_5), .s0(save_1_out_6), .n1(In[1]), .n0(In[0]), .z(z));
endmodule

module transfer (
  input  s1,
  input  s0,
  input  i1,
  input  i0,
  output a1,
  output a0
);

  wire and_1_out, and_2_out, and_3_out, and_4_out, not_1_out, not_2_out, not_3_out, not_4_out, not_5_out,
       not_6_out, not_7_out;

  not not_1 (not_1_out, s1);
  and and_1 (and_1_out, not_1_out, s0, not_2_out);
  not not_2 (not_2_out, i0);
  and and_2 (and_2_out, s1, not_3_out, not_4_out);
  not not_3 (not_3_out, s0);
  not not_4 (not_4_out, i0);
  not not_5 (not_5_out, i1);
  and and_3 (and_3_out, not_5_out, i0);
  and and_4 (and_4_out, s1, not_6_out, not_7_out);
  not not_6 (not_6_out, s0);
  not not_7 (not_7_out, i0);
  or or_1 (a1, and_1_out, and_2_out);
  or or_2 (a0, and_3_out, and_4_out);
endmodule

module save (
  input  in_1,
  input  in_2,
  input  in_3,
  input  in_4,
  output out_5,
  output out_6
);

  wire multiplexer_1_out, multiplexer_2_out;

  Multiplexer multiplexer_1 (.in0(in_1), .in1(1'b0), .out(multiplexer_1_out), .sel(in_3));  // open: en
  Multiplexer multiplexer_2 (.in0(in_2), .in1(1'b0), .out(multiplexer_2_out), .sel(in_3));  // open: en
  Register #(.width(1)) register_1 (.D(multiplexer_1_out), .Q(out_5), .clk(in_4));  // open: en, clr
  Register #(.width(1)) register_2 (.D(multiplexer_2_out), .Q(out_6), .clk(in_4));  // open: en, clr
endmodule

module \output  (
  input  s1,
  input  s0,
  input  n1,
  input  n0,
  output z
);

  wire not_1_out, not_2_out;

  not not_1 (not_1_out, s0);
  and and_1 (z, s1, not_1_out, not_2_out);
  not not_2 (not_2_out, n0);
endmodule
