// Logisim project ftoi.circ as structural Verilog: 6 circuits, main circuit ftoi
module ftoi (
  input  [15:0] in_1,
  output [31:0] out_2
);

  wire comparator_1_lt;
  wire [1:0] checkmode_1_out_2;
  wire [31:0] buma_1_out_2, denormalized_01_1_out_3, multiplexer_1_out, multiplexer_2_out,
       normalized_00_1_out_3;

  Normalized_00 normalized_00_1 (.in_1(in_1[9:0]), .in_2(in_1[14:10]), .out_3(normalized_00_1_out_3));
  Denormalized_01 denormalized_01_1 (.in_1(in_1[9:0]), .in_2(in_1[14:10]), .out_3(denormalized_01_1_out_3));
  CheckMode checkmode_1 (.in_1(in_1[14:10]), .out_2(checkmode_1_out_2));
  Comparator #(.width(5), .mode("unsigned")) comparator_1 (
    .a(in_1[14:10]), .b(5'b01111), .lt(comparator_1_lt));  // open: gt, eq
  Multiplexer #(.select(2), .width(32)) multiplexer_1 (
    .in0(normalized_00_1_out_3), .in1(denormalized_01_1_out_3), .in2({32{1'b0}}), .in3({32{1'b0}}),
    .out(multiplexer_1_out), .sel(checkmode_1_out_2));  // open: en
  Multiplexer #(.width(32)) multiplexer_2 (
    .in0(multiplexer_1_out), .in1({32{1'b0}}), .out(multiplexer_2_out), .sel(comparator_1_lt));  // open: en
  buma buma_1 (.in_1(multiplexer_2_out), .out_2(buma_1_out_2));
  Multiplexer #(.width(32)) multiplexer_3 (
    .in0(multiplexer_2_out), .in1(buma_1_out_2), .out(out_2), .sel(in_1[15]));  // open: en
endmodule

module CheckMode (
  input  [4:0] in_1,
  output [1:0] out_2
);

  wire not_1_out, not_2_out, not_3_out, not_4_out, not_5_out;

  and and_1 (out_2[1], in_1[4], in_1[3], in_1[2], in_1[1], in_1[0]);
  not not_1 (not_1_out, in_1[4]);
  not not_2 (not_2_out, in_1[3]);
  not not_3 (not_3_out, in_1[2]);
  not not_4 (not_4_out, in_1[1]);
  not not_5 (not_5_out, in_1[0]);
  and and_2 (out_2[0], not_1_out, not_2_out, not_3_out, not_4_out, not_5_out);
endmodule

module Normalized_00 (
  input  [9:0] in_1,
  input  [4:0] in_2,
  output [31:0] out_3
);

  wire [4:0] subtractor_1_out;
  wire [31:0] bit_1_1_out_6, bit_extender_1_out, multiplier_1_out, shifter_1_out;

  Subtractor #(.width(5)) subtractor_1 (.a(in_2), .b(5'b01111), .out(subtractor_1_out));  // open: bin, bout
  assign bit_extender_1_out = {{22{1'b0}}, in_1};  // Bit_Extender bit_extender_1
  bit_1 bit_1_1 (
    .in_1(subtractor_1_out[0]), .in_2(subtractor_1_out[1]), .in_3(subtractor_1_out[2]),
    .in_4(subtractor_1_out[3]), .in_5(subtractor_1_out[4]), .out_6(bit_1_1_out_6));
  Multiplier #(.width(32)) multiplier_1 (
    .a(bit_extender_1_out), .b(bit_1_1_out_6), .out(multiplier_1_out));  // open: cin, cout
  Shifter #(.width(32), .shift("lr")) shifter_1 (.in(multiplier_1_out), .\dist (5'b01010), .out(shifter_1_out));
  Adder #(.width(32)) adder_1 (.a(shifter_1_out), .b(bit_1_1_out_6), .out(out_3));  // open: cin, cout
endmodule

module Denormalized_01 (
  input  [9:0] in_1,
  input  [4:0] in_2,
  output [31:0] out_3
);

  wire [4:0] subtractor_1_out;
  wire [31:0] bit_1_1_out_6, bit_extender_1_out, multiplier_1_out;

  Subtractor #(.width(5)) subtractor_1 (.a(in_2), .b(5'b01111), .out(subtractor_1_out));  // open: bin, bout
  assign bit_extender_1_out = {{22{1'b0}}, in_1};  // Bit_Extender bit_extender_1
  bit_1 bit_1_1 (
    .in_1(subtractor_1_out[0]), .in_2(subtractor_1_out[1]), .in_3(subtractor_1_out[2]),
    .in_4(subtractor_1_out[3]), .in_5(subtractor_1_out[4]), .out_6(bit_1_1_out_6));
  Multiplier #(.width(32)) multiplier_1 (
    .a(bit_extender_1_out), .b(bit_1_1_out_6), .out(multiplier_1_out));  // open: cin, cout
  Shifter #(.width(32), .shift("lr")) shifter_1 (.in(multiplier_1_out), .\dist (5'b01010), .out(out_3));
endmodule

module bit_1 (
  input  in_1,
  input  in_2,
  input  in_3,
  input  in_4,
  input  in_5,
  output [31:0] out_6
);

  wire [31:0] multiplexer_1_out, multiplexer_2_out, multiplexer_3_out, multiplexer_4_out, multiplexer_5_out,
       multiplier_1_out, multiplier_2_out, multiplier_3_out;

  Multiplexer #(.width(32)) multiplexer_1 (.in0(32'h1), .in1(32'h2), .out(multiplexer_1_out), .sel(in_1));  // open: en
  Multiplexer #(.width(32)) multiplexer_2 (.in0(32'h1), .in1(32'h4), .out(multiplexer_2_out), .sel(in_2));  // open: en
  Multiplier #(.width(32)) multiplier_1 (
    .a(multiplexer_1_out), .b(multiplexer_2_out), .out(multiplier_1_out));  // open: cin, cout
  Multiplexer #(.width(32)) multiplexer_3 (.in0(32'h1), .in1(32'h10), .out(multiplexer_3_out), .sel(in_3));  // open: en
  Multiplier #(.width(32)) multiplier_2 (
    .a(multiplier_1_out), .b(multiplexer_3_out), .out(multiplier_2_out));  // open: cin, cout
  Multiplexer #(.width(32)) multiplexer_4 (
    .in0(32'h1), .in1(32'h100), .out(multiplexer_4_out), .sel(in_4));  // open: en
  Multiplier #(.width(32)) multiplier_3 (
    .a(multiplier_2_out), .b(multiplexer_4_out), .out(multiplier_3_out));  // open: cin, cout
  Multiplexer #(.width(32)) multiplexer_5 (
    .in0(32'h1), .in1(32'h10000), .out(multiplexer_5_out), .sel(in_5));  // open: en
  Multiplier #(.width(32)) multiplier_4 (.a(multiplier_3_out), .b(multiplexer_5_out), .out(out_6));  // open: cin, cout
endmodule

module buma (
  input  [31:0] in_1,
  output [31:0] out_2
);

  wire [31:0] not_1_out;

  assign not_1_out = ~in_1;  // NOT_Gate not_1, 32 bits wide
  Adder #(.width(32)) adder_1 (.a(not_1_out), .b(32'h1), .out(out_2));  // open: cin, cout
endmodule
