// Logisim project CPU_5.circ as structural Verilog
module main (
  input  in_1,
  output [31:0] out_2,
  output out_3,
  output [4:0] out_4,
  output [31:0] out_5,
  output out_6,
  output [4:0] out_7,
  output [31:0] out_8
);

  wire alu_1_out_5, AluBSel, clk;
  wire [1:0] NPCOp, RegA3Sel;
  wire [2:0] EXTOp, RegDataSel;
  wire [3:0] ALUOp;
  wire [4:0] split_1_out_4, split_1_out_5, split_1_out_6;
  wire [5:0] split_1_out_2, split_1_out_3;
  wire [25:0] split_1_out_7;
  wire [31:0] alu_1_out_4, byte_1_out_3, dm_1_out_6, ext_1_out_4, grf_1_out_8, multiplexer_3_out,
       npc_1_out_6, npc_1_out_7, register_1_q;

  Clock clock_1 (.out(clk));
  // Probe on register_1_q
  NPC npc_1 (
    .PC(register_1_q), .Imm(ext_1_out_4), .in_3(NPCOp), .out_6(npc_1_out_6), .out_7(npc_1_out_7),
    .in_5(alu_1_out_5), .in_4(grf_1_out_8));
  Register #(.width(32)) register_1 (.D(npc_1_out_6), .Q(register_1_q), .clk(clk), .clr(in_1));  // open: en
  IM im_1 (.in_1(register_1_q), .out_2(out_2));
  Split split_1 (
    .in_1(out_2), .out_2(split_1_out_2), .out_4(split_1_out_4), .out_5(split_1_out_5), .out_6(split_1_out_6),
    .out_3(split_1_out_3), .out_7(split_1_out_7));
  Multiplexer #(.select(2), .width(5)) multiplexer_1 (
    .in0(split_1_out_6), .in1(split_1_out_5), .in2({5{1'b1}}), .out(out_4), .sel(RegA3Sel));  // open: in3, en
  EXT ext_1 (.out_4(ext_1_out_4), .in_2(EXTOp), .in_1(split_1_out_7), .in_3(register_1_q[31:28]));
  Multiplexer #(.select(3), .width(32)) multiplexer_2 (
    .in0(alu_1_out_4), .in1(dm_1_out_6), .in2(ext_1_out_4), .in3(npc_1_out_7), .in4(byte_1_out_3),
    .out(out_5), .sel(RegDataSel));  // open: in5, in6, in7, en
  GRF grf_1 (
    .A1(split_1_out_4), .A2(split_1_out_5), .A3(out_4), .WD(out_5), .out_8(grf_1_out_8), .out_9(out_8),
    .WE(out_3), .clk(clk), .resrt(in_1));
  Multiplexer #(.width(32)) multiplexer_3 (
    .in0(out_8), .in1(ext_1_out_4), .out(multiplexer_3_out), .sel(AluBSel));  // open: en
  Controller controller_1 (
    .in_1(split_1_out_3), .in_2(split_1_out_2), .out_3(NPCOp), .out_4(out_3), .out_6(ALUOp), .out_7(out_6),
    .out_8(RegA3Sel), .out_9(RegDataSel), .out_10(AluBSel), .out_5(EXTOp));  // open: out_11
  ALU alu_1 (.in_1(grf_1_out_8), .in_2(multiplexer_3_out), .out_4(alu_1_out_4), .out_5(alu_1_out_5), .in_3(ALUOp));
  _32to5 u_32to5_1 (.in_1(alu_1_out_4), .out_2(out_7));
  \byte  byte_1 (.in_1(dm_1_out_6), .in_2(alu_1_out_4[4:0]), .out_3(byte_1_out_3));
  DM dm_1 (.in_5(out_8), .out_6(dm_1_out_6), .in_4(in_1), .in_2(out_6), .in_3(clk), .in_1(out_7));

  // Other names for the same wires on the sheet: Instr[31:0] = out_2; MemAddr[4:0] = out_7; MemData[31:0] = out_8;
  //   MemWrite = out_6; RegAddr[4:0] = out_4; RegData[31:0] = out_5; RegWrite = out_3; reset = in_1
endmodule

module Split (
  input  [31:0] in_1,
  output [5:0] out_2,
  output [5:0] out_3,
  output [4:0] out_4,
  output [4:0] out_5,
  output [4:0] out_6,
  output [25:0] out_7
);


  assign out_2 = in_1[31:26];
  assign out_3 = in_1[5:0];
  assign out_4 = in_1[25:21];
  assign out_5 = in_1[20:16];
  assign out_6 = in_1[15:11];
  assign out_7 = in_1[25:0];
endmodule

module GRF (
  input  [4:0] A1,
  input  [4:0] A2,
  input  [4:0] A3,
  input  [31:0] WD,
  input  WE,
  input  clk,
  input  resrt,
  output [31:0] out_8,
  output [31:0] out_9
);

  wire W0, W1, W2, W3, W4, W5, W6, W7, W8, W9, W10, W11, W12, W13, W14, W15, W16, W17, W18, W19, W20, W21,
       W22, W23, W24, W25, W26, W27, W28, W29, W30, W31;
  wire [31:0] out0, out1, out2, out3, out4, out5, out6, out7, out8, out9, out10, out11, out12, out13, out14,
       out15, out16, out17, out18, out19, out20, out21, out22, out23, out24, out25, out26, out27, out28,
       out29, out30, out31;

  Demultiplexer #(.select(5)) demultiplexer_1 (
    .out0(W0), .out1(W1), .out2(W2), .out3(W3), .out4(W4), .out5(W5), .out6(W6), .out7(W7), .out8(W8),
    .out9(W9), .out10(W10), .out11(W11), .out12(W12), .out13(W13), .out14(W14), .out15(W15), .out16(W16),
    .out17(W17), .out18(W18), .out19(W19), .out20(W20), .out21(W21), .out22(W22), .out23(W23), .out24(W24),
    .out25(W25), .out26(W26), .out27(W27), .out28(W28), .out29(W29), .out30(W30), .out31(W31), .in(WE),
    .sel(A3));  // open: en
  Register #(.width(32)) register_1 (.D({32{1'b0}}), .en(W0), .Q(out0), .clk(clk), .clr(resrt));
  Register #(.width(32)) register_2 (.D(WD), .en(W1), .Q(out1), .clk(clk), .clr(resrt));
  Register #(.width(32)) register_3 (.D(WD), .en(W2), .Q(out2), .clk(clk), .clr(resrt));
  Register #(.width(32)) register_4 (.D(WD), .en(W3), .Q(out3), .clk(clk), .clr(resrt));
  Register #(.width(32)) register_5 (.D(WD), .en(W4), .Q(out4), .clk(clk), .clr(resrt));
  Register #(.width(32)) register_6 (.D(WD), .en(W5), .Q(out5), .clk(clk), .clr(resrt));
  Register #(.width(32)) register_7 (.D(WD), .en(W6), .Q(out6), .clk(clk), .clr(resrt));
  Register #(.width(32)) register_8 (.D(WD), .en(W7), .Q(out7), .clk(clk), .clr(resrt));
  Register #(.width(32)) register_9 (.D(WD), .en(W8), .Q(out8), .clk(clk), .clr(resrt));
  Register #(.width(32)) register_10 (.D(WD), .en(W9), .Q(out9), .clk(clk), .clr(resrt));
  Register #(.width(32)) register_11 (.D(WD), .en(W10), .Q(out10), .clk(clk), .clr(resrt));
  Register #(.width(32)) register_12 (.D(WD), .en(W11), .Q(out11), .clk(clk), .clr(resrt));
  Register #(.width(32)) register_13 (.D(WD), .en(W12), .Q(out12), .clk(clk), .clr(resrt));
  Register #(.width(32)) register_14 (.D(WD), .en(W13), .Q(out13), .clk(clk), .clr(resrt));
  Register #(.width(32)) register_15 (.D(WD), .en(W14), .Q(out14), .clk(clk), .clr(resrt));
  Register #(.width(32)) register_16 (.D(WD), .en(W15), .Q(out15), .clk(clk), .clr(resrt));
  Register #(.width(32)) register_17 (.D(WD), .en(W16), .Q(out16), .clk(clk), .clr(resrt));
  Register #(.width(32)) register_18 (.D(WD), .en(W17), .Q(out17), .clk(clk), .clr(resrt));
  Register #(.width(32)) register_19 (.D(WD), .en(W18), .Q(out18), .clk(clk), .clr(resrt));
  Register #(.width(32)) register_20 (.D(WD), .en(W19), .Q(out19), .clk(clk), .clr(resrt));
  Register #(.width(32)) register_21 (.D(WD), .en(W20), .Q(out20), .clk(clk), .clr(resrt));
  Register #(.width(32)) register_22 (.D(WD), .en(W21), .Q(out21), .clk(clk), .clr(resrt));
  Register #(.width(32)) register_23 (.D(WD), .en(W22), .Q(out22), .clk(clk), .clr(resrt));
  Register #(.width(32)) register_24 (.D(WD), .en(W23), .Q(out23), .clk(clk), .clr(resrt));
  Register #(.width(32)) register_25 (.D(WD), .en(W24), .Q(out24), .clk(clk), .clr(resrt));
  Register #(.width(32)) register_26 (.D(WD), .en(W25), .Q(out25), .clk(clk), .clr(resrt));
  Register #(.width(32)) register_27 (.D(WD), .en(W26), .Q(out26), .clk(clk), .clr(resrt));
  Register #(.width(32)) register_28 (.D(WD), .en(W27), .Q(out27), .clk(clk), .clr(resrt));
  Register #(.width(32)) register_29 (.D(WD), .en(W28), .Q(out28), .clk(clk), .clr(resrt));
  Register #(.width(32)) register_30 (.D(WD), .en(W29), .Q(out29), .clk(clk), .clr(resrt));
  Register #(.width(32)) register_31 (.D(WD), .en(W30), .Q(out30), .clk(clk), .clr(resrt));
  Register #(.width(32)) register_32 (.D(WD), .en(W31), .Q(out31), .clk(clk), .clr(resrt));
  Multiplexer #(.select(5), .width(32)) multiplexer_1 (
    .in0(out0), .in1(out1), .in2(out2), .in3(out3), .in4(out4), .in5(out5), .in6(out6), .in7(out7),
    .in8(out8), .in9(out9), .in10(out10), .in11(out11), .in12(out12), .in13(out13), .in14(out14),
    .in15(out15), .in16(out16), .in17(out17), .in18(out18), .in19(out19), .in20(out20), .in21(out21),
    .in22(out22), .in23(out23), .in24(out24), .in25(out25), .in26(out26), .in27(out27), .in28(out28),
    .in29(out29), .in30(out30), .in31(out31), .out(out_8), .sel(A1));  // open: en
  Multiplexer #(.select(5), .width(32)) multiplexer_2 (
    .in0(out0), .in1(out1), .in2(out2), .in3(out3), .in4(out4), .in5(out5), .in6(out6), .in7(out7),
    .in8(out8), .in9(out9), .in10(out10), .in11(out11), .in12(out12), .in13(out13), .in14(out14),
    .in15(out15), .in16(out16), .in17(out17), .in18(out18), .in19(out19), .in20(out20), .in21(out21),
    .in22(out22), .in23(out23), .in24(out24), .in25(out25), .in26(out26), .in27(out27), .in28(out28),
    .in29(out29), .in30(out30), .in31(out31), .out(out_9), .sel(A2));  // open: en

  // Other names for the same wires on the sheet: RD1[31:0] = out_8; RD2[31:0] = out_9; reset = resrt
endmodule

module ALU (
  input  [31:0] in_1,
  input  [31:0] in_2,
  input  [3:0] in_3,
  output [31:0] out_4,
  output out_5
);

  wire [31:0] adder_1_out, or_1_out, subtractor_1_out;

  Adder #(.width(32)) adder_1 (.a(in_1), .b(in_2), .out(adder_1_out));  // open: cin, cout
  Subtractor #(.width(32)) subtractor_1 (.a(in_1), .b(in_2), .out(subtractor_1_out));  // open: bin, bout
  assign or_1_out = in_1 | in_2;  // OR_Gate or_1, 32 bits wide
  Comparator #(.width(32)) comparator_1 (.a(in_1), .b(in_2), .eq(out_5));  // open: gt, lt
  Multiplexer #(.select(4), .width(32)) multiplexer_1 (
    .in0(adder_1_out), .in1(subtractor_1_out), .in2(or_1_out), .out(out_4), .sel(in_3));  // open: in3, in4, in5, in6, in7, in8, in9, in10, in11, in12, in13, in14, in15, en
endmodule

module DM (
  input  [4:0] in_1,
  input  in_2,
  input  in_3,
  input  in_4,
  input  [31:0] in_5,
  output [31:0] out_6
);

  RAM #(.addrWidth(5), .dataWidth(32), .bus("separate")) ram_1 (
    .addr(in_1), .din(in_5), .data(out_6), .str(in_2), .clk(in_3), .clr(in_4));  // open: sel, ld
endmodule

module Controller (
  input  [5:0] in_1,
  input  [5:0] in_2,
  output [1:0] out_3,
  output out_4,
  output [2:0] out_5,
  output [3:0] out_6,
  output out_7,
  output [1:0] out_8,
  output [2:0] out_9,
  output out_10,
  output out_11
);

  wire addu_out, beq_out, jal_out, jr_out, lui_out, lw_out, not_1_out, not_2_out, not_3_out, not_4_out,
       not_5_out, not_6_out, not_7_out, not_8_out, not_9_out, not_10_out, not_11_out, not_12_out, ori_out,
       subu_out, sw_out;

  not not_1 (not_1_out, in_1[0]);
  not not_2 (not_2_out, in_1[1]);
  not not_3 (not_3_out, in_1[2]);
  not not_4 (not_4_out, in_1[3]);
  not not_5 (not_5_out, in_1[4]);
  not not_6 (not_6_out, in_1[5]);
  not not_7 (not_7_out, in_2[0]);
  not not_8 (not_8_out, in_2[1]);
  not not_9 (not_9_out, in_2[2]);
  not not_10 (not_10_out, in_2[3]);
  not not_11 (not_11_out, in_2[4]);
  not not_12 (not_12_out, in_2[5]);
  and addu (addu_out, not_12_out, not_11_out, not_10_out, not_9_out, not_8_out, not_7_out, in_1[5], not_5_out, not_4_out, not_3_out, not_2_out, in_1[0]);
  and subu (subu_out, not_12_out, not_11_out, not_10_out, not_9_out, not_8_out, not_7_out, in_1[5], not_5_out, not_4_out, not_3_out, in_1[1], in_1[0]);
  and ori (ori_out, not_12_out, not_11_out, in_2[3], in_2[2], not_8_out, in_2[0]);
  and lw (lw_out, in_2[5], not_11_out, not_10_out, not_9_out, in_2[1], in_2[0]);
  and sw (sw_out, in_2[5], not_11_out, in_2[3], not_9_out, in_2[1], in_2[0]);
  and beq (beq_out, not_12_out, not_11_out, not_10_out, in_2[2], not_8_out, not_7_out);
  and lui (lui_out, not_12_out, not_11_out, in_2[3], in_2[2], in_2[1], in_2[0]);
  and jal (jal_out, not_12_out, not_11_out, not_10_out, not_9_out, in_2[1], in_2[0]);
  and jr (jr_out, not_12_out, not_11_out, not_10_out, not_9_out, not_8_out, not_7_out, not_6_out, not_5_out, in_1[3], not_3_out, not_2_out, not_1_out);
  and lb (out_11, in_2[5], not_11_out, not_10_out, not_9_out, not_8_out, not_7_out);
  or NPCOp1 (out_3[1], jal_out, jr_out);
  or NPCOp0 (out_3[0], beq_out, jr_out);
  or RegWrite (out_4, out_11, addu_out, subu_out, ori_out, lw_out, lui_out, jal_out);
  buf EXTOp2 (out_5[2], jal_out);  // OR_Gate
  or EXTOp1 (out_5[1], lui_out, beq_out);
  or EXTOp0 (out_5[0], lw_out, sw_out, lui_out, out_11);
  buf ALUOp3 (out_6[3], 1'b0);  // OR_Gate
  buf ALUOp2 (out_6[2], 1'b0);  // OR_Gate
  or ALUOp1 (out_6[1], beq_out, ori_out);
  or ALUOp0 (out_6[0], subu_out, beq_out);
  buf MemWrite (out_7, sw_out);  // OR_Gate
  buf RegA3Sel1 (out_8[1], jal_out);  // OR_Gate
  or RegA3Sel0 (out_8[0], ori_out, lw_out, lui_out, out_11);
  buf RegDataSel1 (out_9[2], out_11);  // OR_Gate
  or RegDataSel1_2 (out_9[1], lui_out, jal_out);
  or RegDataSel0 (out_9[0], lw_out, jal_out);
  or AluBSel (out_10, ori_out, lw_out, sw_out, out_11);
endmodule

module NPC (
  input  [31:0] PC,
  input  [31:0] Imm,
  input  [1:0] in_3,
  input  [31:0] in_4,
  input  in_5,
  output [31:0] out_6,
  output [31:0] out_7
);

  wire [31:0] adder_2_out, multiplexer_1_out;

  Adder #(.width(32)) adder_1 (.a(32'h4), .b(PC), .out(out_7));  // open: cin, cout
  Adder #(.width(32)) adder_2 (.a(out_7), .b(Imm), .out(adder_2_out));  // open: cin, cout
  Multiplexer #(.width(32)) multiplexer_1 (
    .in0(out_7), .in1(adder_2_out), .out(multiplexer_1_out), .sel(in_5));  // open: en
  Multiplexer #(.select(2), .width(32)) multiplexer_2 (
    .in0(out_7), .in1(multiplexer_1_out), .in2(Imm), .in3(in_4), .out(out_6), .sel(in_3));  // open: en
endmodule

module IM (
  input  [31:0] in_1,
  output [31:0] out_2
);

  wire [4:0] n32to5_1_out_2;

  _32to5 u_32to5_1 (.in_1(in_1), .out_2(n32to5_1_out_2));
  ROM #(.addrWidth(5), .dataWidth(32)) rom_1 (.addr(n32to5_1_out_2), .data(out_2));  // open: sel

  // Notes on the sheet:
  //   contents of rom_1 (hex, n*v repeats v):
  //   34011234 34020040 340a0004 ac410000 80430000 80440001 80450002 80460003 4a3821 80e8fffd
endmodule

module EXT (
  input  [25:0] in_1,
  input  [2:0] in_2,
  input  [3:0] in_3,
  output [31:0] out_4
);

  wire [27:0] bit_extender_1_out, shifter_1_out;
  wire [31:0] bit_extender_2_out, bit_extender_3_out, bit_extender_4_out;

  assign bit_extender_1_out = {{2{1'b0}}, in_1};  // Bit_Extender bit_extender_1
  Shifter #(.width(28)) shifter_1 (.in(bit_extender_1_out), .\dist (5'b00010), .out(shifter_1_out));
  assign bit_extender_2_out = {{16{1'b0}}, in_1[15:0]};  // Bit_Extender bit_extender_2
  assign bit_extender_3_out = {{16{in_1[15]}}, in_1[15:0]};  // Bit_Extender bit_extender_3
  assign bit_extender_4_out = {{14{in_1[15]}}, {in_1[15:0], 2'b00}};  // Bit_Extender bit_extender_4
  Multiplexer #(.select(3), .width(32)) multiplexer_1 (
    .in0(bit_extender_2_out), .in1(bit_extender_3_out), .in2(bit_extender_4_out),
    .in3({in_1[15:0], {16{1'b0}}}), .in4({in_3, shifter_1_out}), .out(out_4), .sel(in_2));  // open: in5, in6, in7, en
endmodule

module _32to5 (
  input  [31:0] in_1,
  output [4:0] out_2
);


  assign out_2 = in_1[6:2];
endmodule

module \byte  (
  input  [31:0] in_1,
  input  [4:0] in_2,
  output [31:0] out_3
);

  wire [7:0] multiplexer_1_out;

  Multiplexer #(.select(2), .width(8)) multiplexer_1 (
    .in0(in_1[7:0]), .in1(in_1[15:8]), .in2(in_1[23:16]), .in3(in_1[31:24]), .out(multiplexer_1_out),
    .sel(in_2[1:0]));  // open: en
  assign out_3 = {{24{multiplexer_1_out[7]}}, multiplexer_1_out};  // Bit_Extender bit_extender_1
endmodule
