// Logisim project 斐波那契1.circ as structural Verilog: 1 circuit, main circuit main
module main (
  input  [2:0] in_1,
  output [3:0] out_2
);

  wire clock_1_out, comparator_1_eq, comparator_2_eq, not_1_out;
  wire [2:0] counter_1_q;
  wire [3:0] adder_1_out, multiplexer_1_out, multiplexer_2_out, multiplexer_3_out, register_1_q,
       register_2_q, register_3_q;

  Multiplexer #(.width(4)) multiplexer_1 (
    .in0(register_2_q), .in1(4'b0001), .out(multiplexer_1_out), .sel(comparator_1_eq));  // open: en
  Multiplexer #(.width(4)) multiplexer_2 (
    .in0(adder_1_out), .in1(4'b0001), .out(multiplexer_2_out), .sel(comparator_1_eq));  // open: en
  Register #(.width(4)) register_1 (.D(multiplexer_1_out), .Q(register_1_q), .clk(clock_1_out));  // open: en, clr
  Adder #(.width(4)) adder_1 (.a(register_1_q), .b(register_2_q), .out(adder_1_out));  // open: cin, cout
  Register #(.width(4)) register_2 (.D(multiplexer_2_out), .Q(register_2_q), .clk(clock_1_out));  // open: en, clr
  Counter #(.width(3), .max('h7)) counter_1 (.Q(counter_1_q), .clk(clock_1_out));  // open: load, D, count, carry, clr
  Clock clock_1 (.out(clock_1_out));
  Comparator #(.width(3)) comparator_1 (.a(3'b000), .b(counter_1_q), .eq(comparator_1_eq));  // open: gt, lt
  Comparator #(.width(3)) comparator_2 (.a(in_1), .b(counter_1_q), .eq(comparator_2_eq));  // open: gt, lt
  Multiplexer #(.width(4)) multiplexer_3 (
    .in0(4'b0000), .in1(register_1_q), .out(multiplexer_3_out), .sel(comparator_2_eq));  // open: en
  Register #(.width(4)) register_3 (
    .D(multiplexer_3_out), .en(comparator_2_eq), .Q(register_3_q), .clk(clock_1_out));  // open: clr
  Multiplexer #(.width(4)) multiplexer_4 (
    .in0(multiplexer_3_out), .in1(register_3_q), .out(out_2), .sel(not_1_out));  // open: en
  not not_1 (not_1_out, comparator_2_eq);
endmodule
