// Logisim project 斐波那契2.circ as structural Verilog: 8 circuits, main circuit 平方
module \平方  (
  input  [31:0] a11,
  input  [31:0] a12,
  input  [31:0] a21,
  input  [31:0] a22,
  output [31:0] b11,
  output [31:0] b12,
  output [31:0] b21,
  output [31:0] b22
);

  wire [31:0] adder_1_out, multiplier_1_out, multiplier_2_out, multiplier_3_out;

  Multiplier #(.width(32)) multiplier_1 (.a(a11), .b(a11), .out(multiplier_1_out));  // open: cin, cout
  Multiplier #(.width(32)) multiplier_2 (.a(a12), .b(a21), .out(multiplier_2_out));  // open: cin, cout
  Adder #(.width(32)) adder_1 (.a(a11), .b(a22), .out(adder_1_out));  // open: cin, cout
  Multiplier #(.width(32)) multiplier_3 (.a(a22), .b(a22), .out(multiplier_3_out));  // open: cin, cout
  Adder #(.width(32)) adder_2 (.a(multiplier_1_out), .b(multiplier_2_out), .out(b11));  // open: cin, cout
  Multiplier #(.width(32)) multiplier_4 (.a(a12), .b(adder_1_out), .out(b12));  // open: cin, cout
  Multiplier #(.width(32)) multiplier_5 (.a(adder_1_out), .b(a21), .out(b21));  // open: cin, cout
  Adder #(.width(32)) adder_3 (.a(multiplier_2_out), .b(multiplier_3_out), .out(b22));  // open: cin, cout
endmodule

module \判断起始  (
  input  [31:0] in_1,
  input  [31:0] in_2,
  input  [31:0] in_3,
  input  [31:0] in_4,
  input  [31:0] in_5,
  input  [31:0] in_6,
  input  [31:0] in_7,
  input  [31:0] in_8,
  input  in_9,
  output [31:0] out_10,
  output [31:0] out_11,
  output [31:0] out_12,
  output [31:0] out_13,
  output out_14
);

  wire comparator_1_eq;
  wire [31:0] or_1_out;

  assign or_1_out = in_2 | in_4 | in_5 | in_7;  // OR_Gate or_1, 32 bits wide
  Comparator #(.width(32)) comparator_1 (.a(or_1_out), .b({32{1'b0}}), .eq(comparator_1_eq));  // open: gt, lt
  and and_1 (out_14, comparator_1_eq, in_9);
  Multiplexer #(.width(32)) multiplexer_1 (.in0(in_1), .in1(32'h1), .out(out_10), .sel(out_14));  // open: en
  Multiplexer #(.width(32)) multiplexer_2 (.in0(in_3), .in1(32'h1), .out(out_11), .sel(out_14));  // open: en
  Multiplexer #(.width(32)) multiplexer_3 (.in0(in_6), .in1(32'h1), .out(out_12), .sel(out_14));  // open: en
  Multiplexer #(.width(32)) multiplexer_4 (.in0(in_8), .in1({32{1'b0}}), .out(out_13), .sel(out_14));  // open: en
endmodule

module main (
  input  [31:0] in_1,
  output [31:0] out_2
);

  wire clock_1_out, comparator_1_eq, comparator_2_eq, comparator_3_eq, multiplexer_1_out, not_1_out,
       \判断第一个1_out_14 ;
  wire [4:0] counter_1_q;
  wire [31:0] adder_1_out, multiplexer_2_out, multiplexer_3_out, multiplexer_4_out, multiplexer_5_out,
       multiplexer_6_out, multiplexer_7_out, multiplexer_8_out, multiplexer_9_out, multiplexer_10_out,
       multiplexer_11_out, register_1_q, register_2_q, register_3_q, register_4_q, \减一_out_2 ,
       \判断第一个1_out_10 , \判断第一个1_out_11 , \判断第一个1_out_12 , \判断第一个1_out_13 , \到头锁住_q , \平方_b11 , \平方_b12 ,
       \平方_b21 , \平方_b22 , \平方加一_out_5 , \平方加一_out_6 , \平方加一_out_7 , \平方加一_out_8 , \归零_1_out_10 ,
       \归零_1_out_11 , \归零_1_out_12 , \归零_1_out_13 , \归零_1_out_14 , \归零_1_out_15 , \归零_1_out_16 ,
       \归零_1_out_17 , \把1搞掉_out_2 ;

  \特殊的1  \u_把1搞掉  (.in_1(in_1), .out_2(\把1搞掉_out_2 ));
  \初始化  \u_减一  (.in_1(\把1搞掉_out_2 ), .out_2(\减一_out_2 ));
  Counter #(.width(5), .max('h1f)) counter_1 (.Q(counter_1_q), .clk(clock_1_out));  // open: load, D, count, carry, clr
  Clock clock_1 (.out(clock_1_out));
  Multiplexer #(.select(5)) multiplexer_1 (
    .in0(\减一_out_2 [31]), .in1(\减一_out_2 [30]), .in2(\减一_out_2 [29]), .in3(\减一_out_2 [28]),
    .in4(\减一_out_2 [27]), .in5(\减一_out_2 [26]), .in6(\减一_out_2 [25]), .in7(\减一_out_2 [24]),
    .in8(\减一_out_2 [23]), .in9(\减一_out_2 [22]), .in10(\减一_out_2 [21]), .in11(\减一_out_2 [20]),
    .in12(\减一_out_2 [19]), .in13(\减一_out_2 [18]), .in14(\减一_out_2 [17]), .in15(\减一_out_2 [16]),
    .in16(\减一_out_2 [15]), .in17(\减一_out_2 [14]), .in18(\减一_out_2 [13]), .in19(\减一_out_2 [12]),
    .in20(\减一_out_2 [11]), .in21(\减一_out_2 [10]), .in22(\减一_out_2 [9]), .in23(\减一_out_2 [8]),
    .in24(\减一_out_2 [7]), .in25(\减一_out_2 [6]), .in26(\减一_out_2 [5]), .in27(\减一_out_2 [4]),
    .in28(\减一_out_2 [3]), .in29(\减一_out_2 [2]), .in30(\减一_out_2 [1]), .in31(\减一_out_2 [0]),
    .out(multiplexer_1_out), .sel(counter_1_q));  // open: en
  Comparator #(.width(5)) comparator_1 (.a(counter_1_q), .b({5{1'b0}}), .eq(comparator_1_eq));  // open: gt, lt
  \归零  \u_归零_1  (
    .in_1(register_1_q), .in_2(register_2_q), .in_3(register_3_q), .in_4(register_4_q), .in_5(register_1_q),
    .in_6(register_2_q), .in_7(register_3_q), .in_8(register_4_q), .in_9(comparator_1_eq),
    .out_10(\归零_1_out_10 ), .out_11(\归零_1_out_11 ), .out_12(\归零_1_out_12 ), .out_13(\归零_1_out_13 ),
    .out_14(\归零_1_out_14 ), .out_15(\归零_1_out_15 ), .out_16(\归零_1_out_16 ), .out_17(\归零_1_out_17 ));
  \判断起始  \u_判断第一个1  (
    .in_1(\归零_1_out_14 ), .in_2(\归零_1_out_10 ), .in_3(\归零_1_out_15 ), .in_4(\归零_1_out_11 ),
    .in_5(\归零_1_out_12 ), .in_6(\归零_1_out_16 ), .in_7(\归零_1_out_13 ), .in_8(\归零_1_out_17 ),
    .in_9(multiplexer_1_out), .out_10(\判断第一个1_out_10 ), .out_11(\判断第一个1_out_11 ), .out_12(\判断第一个1_out_12 ),
    .out_13(\判断第一个1_out_13 ), .out_14(\判断第一个1_out_14 ));
  // Probe on multiplexer_1_out
  \平方加一  \u_平方加一  (
    .in_1(\判断第一个1_out_10 ), .in_2(\判断第一个1_out_11 ), .in_3(\判断第一个1_out_12 ), .in_4(\判断第一个1_out_13 ),
    .out_5(\平方加一_out_5 ), .out_6(\平方加一_out_6 ), .out_7(\平方加一_out_7 ), .out_8(\平方加一_out_8 ));
  Multiplexer #(.width(32)) multiplexer_2 (
    .in0(\平方加一_out_5 ), .in1(\判断第一个1_out_10 ), .out(multiplexer_2_out), .sel(\判断第一个1_out_14 ));  // open: en
  Multiplexer #(.width(32)) multiplexer_3 (
    .in0(\平方加一_out_6 ), .in1(\判断第一个1_out_11 ), .out(multiplexer_3_out), .sel(\判断第一个1_out_14 ));  // open: en
  Multiplexer #(.width(32)) multiplexer_4 (
    .in0(\平方加一_out_7 ), .in1(\判断第一个1_out_12 ), .out(multiplexer_4_out), .sel(\判断第一个1_out_14 ));  // open: en
  Multiplexer #(.width(32)) multiplexer_5 (
    .in0(\平方加一_out_8 ), .in1(\判断第一个1_out_13 ), .out(multiplexer_5_out), .sel(\判断第一个1_out_14 ));  // open: en
  Comparator #(.width(5)) comparator_2 (.a(counter_1_q), .b({5{1'b1}}), .eq(comparator_2_eq));  // open: gt, lt
  Comparator #(.width(1)) comparator_3 (.a(1'b1), .b(multiplexer_1_out), .eq(comparator_3_eq));  // open: gt, lt
  \平方  \u_平方  (
    .a11(register_1_q), .a12(register_2_q), .a21(register_3_q), .a22(register_4_q), .b11(\平方_b11 ),
    .b12(\平方_b12 ), .b21(\平方_b21 ), .b22(\平方_b22 ));
  Register #(.width(32)) register_1 (.D(multiplexer_6_out), .Q(register_1_q), .clk(clock_1_out));  // open: en, clr
  Multiplexer #(.width(32)) multiplexer_6 (
    .in0(\平方_b11 ), .in1(multiplexer_2_out), .out(multiplexer_6_out), .sel(comparator_3_eq));  // open: en
  Register #(.width(32)) register_2 (.D(multiplexer_7_out), .Q(register_2_q), .clk(clock_1_out));  // open: en, clr
  Multiplexer #(.width(32)) multiplexer_7 (
    .in0(\平方_b12 ), .in1(multiplexer_3_out), .out(multiplexer_7_out), .sel(comparator_3_eq));  // open: en
  Multiplexer #(.width(32)) multiplexer_8 (
    .in0(\平方_b21 ), .in1(multiplexer_4_out), .out(multiplexer_8_out), .sel(comparator_3_eq));  // open: en
  Register #(.width(32)) register_3 (.D(multiplexer_8_out), .Q(register_3_q), .clk(clock_1_out));  // open: en, clr
  Register #(.width(32)) register_4 (.D(multiplexer_9_out), .Q(register_4_q), .clk(clock_1_out));  // open: en, clr
  Multiplexer #(.width(32)) multiplexer_9 (
    .in0(\平方_b22 ), .in1(multiplexer_5_out), .out(multiplexer_9_out), .sel(comparator_3_eq));  // open: en
  Multiplexer #(.width(32)) multiplexer_10 (
    .in0({32{1'b0}}), .in1(multiplexer_8_out), .out(multiplexer_10_out), .sel(comparator_2_eq));  // open: en
  Multiplexer #(.width(32)) multiplexer_11 (
    .in0({32{1'b0}}), .in1(multiplexer_9_out), .out(multiplexer_11_out), .sel(comparator_2_eq));  // open: en
  Adder #(.width(32)) adder_1 (.a(multiplexer_10_out), .b(multiplexer_11_out), .out(adder_1_out));  // open: cin, cout
  not not_1 (not_1_out, comparator_2_eq);
  Multiplexer #(.width(32)) multiplexer_12 (
    .in0(adder_1_out), .in1(\到头锁住_q ), .out(out_2), .sel(not_1_out));  // open: en
  Register #(.width(32)) \u_到头锁住  (
    .D(adder_1_out), .en(comparator_2_eq), .Q(\到头锁住_q ), .clk(clock_1_out));  // open: clr

  // Notes on the sheet:
  //   如果是第一个1，初始化，如果不是，从寄存器中的值开始平方加一
  //   如果这一位是1，把平方加一传出去，如果是0，把平方传出去
  //   没到头，用寄存器，到头了寄存器存一个值。第一个周期寄存器是0，第一个周期结束，寄存器总是结果值
endmodule

module \平方加一  (
  input  [31:0] in_1,
  input  [31:0] in_2,
  input  [31:0] in_3,
  input  [31:0] in_4,
  output [31:0] out_5,
  output [31:0] out_6,
  output [31:0] out_7,
  output [31:0] out_8
);

  wire [31:0] \平方_1_b11 , \平方_1_b12 , \平方_1_b21 , \平方_1_b22 ;

  \平方  \u_平方_1  (
    .a11(in_1), .a12(in_2), .a21(in_3), .a22(in_4), .b11(\平方_1_b11 ), .b12(\平方_1_b12 ), .b21(\平方_1_b21 ),
    .b22(\平方_1_b22 ));
  \加加一  \u_加加一_1  (
    .in_1(\平方_1_b11 ), .in_2(\平方_1_b12 ), .in_3(\平方_1_b21 ), .in_4(\平方_1_b22 ), .out_5(out_5), .out_6(out_6),
    .out_7(out_7), .out_8(out_8));
endmodule

module \加加一  (
  input  [31:0] in_1,
  input  [31:0] in_2,
  input  [31:0] in_3,
  input  [31:0] in_4,
  output [31:0] out_5,
  output [31:0] out_6,
  output [31:0] out_7,
  output [31:0] out_8
);

  Adder #(.width(32)) adder_1 (.a(in_1), .b(in_3), .out(out_5));  // open: cin, cout
  Adder #(.width(32)) adder_2 (.a(in_2), .b(in_4), .out(out_6));  // open: cin, cout

  assign out_7 = in_1;
  assign out_8 = in_2;
endmodule

module \初始化  (
  input  [31:0] in_1,
  output [31:0] out_2
);

  wire comparator_1_eq;
  wire [31:0] subtractor_1_out;

  Subtractor #(.width(32)) subtractor_1 (.a(in_1), .b(32'h1), .out(subtractor_1_out));  // open: bin, bout
  Multiplexer #(.width(32)) multiplexer_1 (
    .in0(subtractor_1_out), .in1(in_1), .out(out_2), .sel(comparator_1_eq));  // open: en
  Comparator #(.width(32)) comparator_1 (.a(in_1), .b({32{1'b0}}), .eq(comparator_1_eq));  // open: gt, lt
endmodule

module \特殊的1  (
  input  [31:0] in_1,
  output [31:0] out_2
);

  wire comparator_1_eq;
  wire [31:0] adder_1_out;

  Adder #(.width(32)) adder_1 (.a(32'h1), .b(in_1), .out(adder_1_out));  // open: cin, cout
  Comparator #(.width(32)) comparator_1 (.a(in_1), .b(32'h1), .eq(comparator_1_eq));  // open: gt, lt
  Multiplexer #(.width(32)) multiplexer_1 (
    .in0(in_1), .in1(adder_1_out), .out(out_2), .sel(comparator_1_eq));  // open: en
endmodule

module \归零  (
  input  [31:0] in_1,
  input  [31:0] in_2,
  input  [31:0] in_3,
  input  [31:0] in_4,
  input  [31:0] in_5,
  input  [31:0] in_6,
  input  [31:0] in_7,
  input  [31:0] in_8,
  input  in_9,
  output [31:0] out_10,
  output [31:0] out_11,
  output [31:0] out_12,
  output [31:0] out_13,
  output [31:0] out_14,
  output [31:0] out_15,
  output [31:0] out_16,
  output [31:0] out_17
);

  Multiplexer #(.width(32)) multiplexer_1 (.in0(in_1), .in1({32{1'b0}}), .out(out_10), .sel(in_9));  // open: en
  Multiplexer #(.width(32)) multiplexer_2 (.in0(in_2), .in1({32{1'b0}}), .out(out_11), .sel(in_9));  // open: en
  Multiplexer #(.width(32)) multiplexer_3 (.in0(in_3), .in1({32{1'b0}}), .out(out_12), .sel(in_9));  // open: en
  Multiplexer #(.width(32)) multiplexer_4 (.in0(in_4), .in1({32{1'b0}}), .out(out_13), .sel(in_9));  // open: en
  Multiplexer #(.width(32)) multiplexer_5 (.in0(in_5), .in1({32{1'b0}}), .out(out_14), .sel(in_9));  // open: en
  Multiplexer #(.width(32)) multiplexer_6 (.in0(in_6), .in1({32{1'b0}}), .out(out_15), .sel(in_9));  // open: en
  Multiplexer #(.width(32)) multiplexer_7 (.in0(in_7), .in1({32{1'b0}}), .out(out_16), .sel(in_9));  // open: en
  Multiplexer #(.width(32)) multiplexer_8 (.in0(in_8), .in1({32{1'b0}}), .out(out_17), .sel(in_9));  // open: en
endmodule
