// Logisim project mod5.circ as structural Verilog: 3 circuits, main circuit mod5
module mod5 (
  input  in_1,
  output out_2,
  output out_3,
  output out_4,
  output out_5,
  output out_6
);

  wire clock_1_out, register_1_q, register_2_q, \状态_1_s10 , \状态_1_s11 ;

  Clock clock_1 (.out(clock_1_out));
  \状态  \u_状态_1  (.s01(register_1_q), .s00(register_2_q), .In(in_1), .s11(\状态_1_s11 ), .s10(\状态_1_s10 ));
  Register #(.width(1)) register_1 (.D(\状态_1_s11 ), .Q(register_1_q), .clk(clock_1_out));  // open: en, clr
  Register #(.width(1)) register_2 (.D(\状态_1_s10 ), .Q(register_2_q), .clk(clock_1_out));  // open: en, clr
  \输出  \u_输出_1  (.s01(\状态_1_s11 ), .s00(\状态_1_s10 ), .s0(out_2), .s1(out_3), .s2(out_4), .s3(out_5), .s4(out_6));
endmodule

module \状态  (
  input  s01,
  input  s00,
  input  In,
  output s11,
  output s10
);

  wire and_1_out, and_2_out, and_3_out, and_4_out, and_5_out, and_6_out, not_1_out, not_2_out, not_3_out,
       not_4_out, not_5_out, not_6_out, not_7_out, not_8_out;

  not not_1 (not_1_out, s01);
  not not_2 (not_2_out, s00);
  not not_3 (not_3_out, s01);
  not not_4 (not_4_out, s00);
  not not_5 (not_5_out, s01);
  not not_6 (not_6_out, In);
  not not_7 (not_7_out, s00);
  not not_8 (not_8_out, In);
  and and_1 (and_1_out, not_1_out, s00);
  and and_2 (and_2_out, s01, not_2_out);
  and and_3 (and_3_out, not_3_out, not_4_out, In);
  and and_4 (and_4_out, not_5_out, s00, not_6_out);
  and and_5 (and_5_out, s01, not_7_out, not_8_out);
  and and_6 (and_6_out, s01, s00, In);
  or or_1 (s11, and_1_out, and_2_out);
  or or_2 (s10, and_3_out, and_4_out, and_5_out, and_6_out);
endmodule

module \输出  (
  input  s01,
  input  s00,
  output s0,
  output s1,
  output s2,
  output s3,
  output s4
);

  wire not_1_out, not_2_out, not_3_out, not_4_out;

  not not_1 (not_1_out, s01);
  not not_2 (not_2_out, s00);
  not not_3 (not_3_out, s01);
  not not_4 (not_4_out, s00);
  and and_1 (s4, s01, s00);
  and and_2 (s1, not_1_out, not_2_out);
  and and_3 (s2, not_3_out, s00);
  and and_4 (s3, s01, not_4_out);

  assign s0 = 1'b0;
endmodule
